// Logisim project Proj2starter.circ as structural Verilog: 4 circuits, main circuit regfile
module CPUmain (
  input  [31:0] in_1
);

  wire control_1_imm_sel, control_1_reg_write_e, undriven, undriven_2;
  wire [3:0] control_1_alu_code;
  wire [4:0] control_1_rd, control_1_rs, control_1_rt;
  wire [15:0] bit_extender_1_out;
  wire [31:0] alu_1_res, control_1_imm, multiplexer_1_out, multiplexer_2_out, ram_1_dout, regfile_1_rs_data,
       regfile_1_rt_data, shifter_1_out;

  ROM #(.addrWidth(16), .dataWidth(32)) rom_1 ();  // open: addr, data
  Multiplexer #(.width(32)) multiplexer_1 (.in0(alu_1_res), .in1(ram_1_dout), .out(multiplexer_1_out), .sel(undriven));
  regfile regfile_1 (
    .rd_data(multiplexer_1_out), .rd(control_1_rd), .write_e(control_1_reg_write_e), .rs(control_1_rs),
    .rt(control_1_rt), .rs_data(regfile_1_rs_data), .rt_data(regfile_1_rt_data));
  Control control_1 (
    .Inst(in_1), .rs(control_1_rs), .rt(control_1_rt), .rd(control_1_rd), .imm(control_1_imm),
    .reg_write_e(control_1_reg_write_e), .imm_sel(control_1_imm_sel), .ALU_code(control_1_alu_code));
  Multiplexer #(.width(32)) multiplexer_2 (
    .in0(regfile_1_rt_data), .in1(control_1_imm), .out(multiplexer_2_out), .sel(control_1_imm_sel));
  Shifter #(.shift("lr"), .width(32)) shifter_1 (.in(alu_1_res), .out(shifter_1_out));  // open: dist
  ALU alu_1 (.OP1(regfile_1_rs_data), .OP2(multiplexer_2_out), .ALU_CODE(control_1_alu_code), .Res(alu_1_res));
  Bit_Extender #(.in_width(32)) bit_extender_1 (.in(shifter_1_out), .out(bit_extender_1_out));
  RAM #(.addrWidth(16), .dataWidth(32)) ram_1 (
    .addr(bit_extender_1_out), .we(undriven_2), .clk(1'b1), .dout(ram_1_dout));  // open: oe, din
  // Pins of 1 and 3 bits meet at 3'b101
endmodule

module regfile (
  input  [4:0] rd,
  input  write_e,
  input  [4:0] rs,
  input  [4:0] rt,
  input  [31:0] rd_data,
  output [31:0] rs_data,
  output [31:0] rt_data
);
endmodule

module ALU (
  input  [3:0] ALU_CODE,
  input  [31:0] OP1,
  input  [31:0] OP2,
  output [31:0] Res
);

  Adder adder_1 ();  // open: a, b, out, cin, cout
  Subtractor subtractor_1 ();  // open: a, b, out, bin, bout
  Multiplier multiplier_1 ();  // open: a, b, out, cin, cout
  Divider divider_1 ();  // open: a, b, out, upper, rem
  Register HI ();  // open: D, en, clk, Q, clr
  Register LO ();  // open: D, en, clk, Q, clr
endmodule

module Control (
  input  [31:0] Inst,
  output [4:0] rs,
  output [4:0] rt,
  output [4:0] rd,
  output [31:0] imm,
  output reg_write_e,
  output imm_sel,
  output [3:0] ALU_code
);
endmodule
