// Logisim project Project2.circ as structural Verilog: 4 circuits, main circuit regfile
module CPUmain (
  input  [31:0] in_1
);

  wire control_1_imm_sel, control_1_reg_write_e, undriven, undriven_2;
  wire [3:0] control_1_alu_code;
  wire [4:0] control_1_rd, control_1_rs, control_1_rt;
  wire [15:0] bit_extender_1_out;
  wire [31:0] alu_1_p3, control_1_imm, multiplexer_1_out, multiplexer_2_out, ram_1_dout, regfile_1_rs_data,
       regfile_1_rt_data, shifter_1_out;

  ROM #(.addrWidth(16), .dataWidth(32)) rom_1 ();  // open: addr, data
  Multiplexer #(.width(32)) multiplexer_1 (.in0(alu_1_p3), .in1(ram_1_dout), .out(multiplexer_1_out), .sel(undriven));
  regfile regfile_1 (
    .rd(control_1_rd), .rt(control_1_rt), .rs(control_1_rs), .write_e(control_1_reg_write_e),
    .rd_data(multiplexer_1_out), .rs_data(regfile_1_rs_data), .rt_data(regfile_1_rt_data));
  Control control_1 (
    .Inst(in_1), .rs(control_1_rs), .rt(control_1_rt), .rd(control_1_rd), .imm(control_1_imm),
    .reg_write_e(control_1_reg_write_e), .imm_sel(control_1_imm_sel), .ALU_code(control_1_alu_code));
  Multiplexer #(.width(32)) multiplexer_2 (
    .in0(regfile_1_rt_data), .in1(control_1_imm), .out(multiplexer_2_out), .sel(control_1_imm_sel));
  // ALU alu_1: pin names not known; wires that end beside it: regfile_1_rs_data, control_1_alu_code, alu_1_p3
  Shifter #(.shift("lr"), .width(32)) shifter_1 (.in(alu_1_p3), .out(shifter_1_out));  // open: dist
  Bit_Extender #(.in_width(32)) bit_extender_1 (.in(shifter_1_out), .out(bit_extender_1_out));
  RAM #(.addrWidth(16), .dataWidth(32)) ram_1 (
    .addr(bit_extender_1_out), .we(undriven_2), .clk(1'b1), .dout(ram_1_dout));  // open: oe, din
  // Pins of 1 and 3 bits meet at 3'b101
endmodule

module regfile (
  input  [31:0] rd_data,
  input  write_e,
  input  [4:0] rs,
  input  [4:0] rd,
  input  [4:0] rt,
  output [31:0] rs_data,
  output [31:0] rt_data
);

  wire and_1_out, and_2_out, and_3_out, and_4_out, and_5_out, and_6_out, and_7_out, and_8_out, and_9_out,
       and_10_out, and_11_out, and_12_out, and_13_out, and_14_out, and_15_out, and_16_out, and_17_out,
       and_18_out, and_19_out, and_20_out, and_21_out, and_22_out, and_23_out, and_24_out, and_25_out,
       and_26_out, and_27_out, and_28_out, and_29_out, and_30_out, and_31_out, clock_1_out,
       demultiplexer_1_out1, demultiplexer_1_out2, demultiplexer_1_out3, demultiplexer_1_out4,
       demultiplexer_1_out5, demultiplexer_1_out6, demultiplexer_1_out7, demultiplexer_1_out8,
       demultiplexer_1_out9, demultiplexer_1_out10, demultiplexer_1_out11, demultiplexer_1_out12,
       demultiplexer_1_out13, demultiplexer_1_out14, demultiplexer_1_out15, demultiplexer_1_out16,
       demultiplexer_1_out17, demultiplexer_1_out18, demultiplexer_1_out19, demultiplexer_1_out20,
       demultiplexer_1_out21, demultiplexer_1_out22, demultiplexer_1_out23, demultiplexer_1_out24,
       demultiplexer_1_out25, demultiplexer_1_out26, demultiplexer_1_out27, demultiplexer_1_out28,
       demultiplexer_1_out29, demultiplexer_1_out30, demultiplexer_1_out31;
  wire [31:0] register_1_q, register_2_q, register_3_q, register_4_q, register_5_q, register_6_q,
       register_7_q, register_8_q, register_9_q, register_10_q, register_11_q, register_12_q, register_13_q,
       register_14_q, register_15_q, register_16_q, register_17_q, register_18_q, register_19_q,
       register_20_q, register_21_q, register_22_q, register_23_q, register_24_q, register_25_q,
       register_26_q, register_27_q, register_28_q, register_29_q, register_30_q, register_31_q;

  Demultiplexer #(.select(5)) demultiplexer_1 (
    .out1(demultiplexer_1_out1), .out2(demultiplexer_1_out2), .out3(demultiplexer_1_out3),
    .out4(demultiplexer_1_out4), .out5(demultiplexer_1_out5), .out6(demultiplexer_1_out6),
    .out7(demultiplexer_1_out7), .out8(demultiplexer_1_out8), .out9(demultiplexer_1_out9),
    .out10(demultiplexer_1_out10), .out11(demultiplexer_1_out11), .out12(demultiplexer_1_out12),
    .out13(demultiplexer_1_out13), .out14(demultiplexer_1_out14), .out15(demultiplexer_1_out15),
    .out16(demultiplexer_1_out16), .out17(demultiplexer_1_out17), .out18(demultiplexer_1_out18),
    .out19(demultiplexer_1_out19), .out20(demultiplexer_1_out20), .out21(demultiplexer_1_out21),
    .out22(demultiplexer_1_out22), .out23(demultiplexer_1_out23), .out24(demultiplexer_1_out24),
    .out25(demultiplexer_1_out25), .out26(demultiplexer_1_out26), .out27(demultiplexer_1_out27),
    .out28(demultiplexer_1_out28), .out29(demultiplexer_1_out29), .out30(demultiplexer_1_out30),
    .out31(demultiplexer_1_out31), .in(1'b1), .sel(rd));  // open: out0
  Clock clock_1 (.out(clock_1_out));
  and and_1 (and_1_out, write_e, demultiplexer_1_out1);
  and and_2 (and_2_out, write_e, demultiplexer_1_out5);
  and and_3 (and_3_out, write_e, demultiplexer_1_out9);
  and and_4 (and_4_out, write_e, demultiplexer_1_out13);
  and and_5 (and_5_out, write_e, demultiplexer_1_out17);
  and and_6 (and_6_out, write_e, demultiplexer_1_out21);
  and and_7 (and_7_out, write_e, demultiplexer_1_out25);
  and and_8 (and_8_out, write_e, demultiplexer_1_out29);
  Register #(.width(32)) register_1 (.D(rd_data), .en(and_1_out), .clk(clock_1_out), .Q(register_1_q));  // open: clr
  Register #(.width(32)) register_2 (.D(rd_data), .en(and_2_out), .clk(clock_1_out), .Q(register_2_q));  // open: clr
  Register #(.width(32)) register_3 (.D(rd_data), .en(and_3_out), .clk(clock_1_out), .Q(register_3_q));  // open: clr
  Register #(.width(32)) register_4 (.D(rd_data), .en(and_4_out), .clk(clock_1_out), .Q(register_4_q));  // open: clr
  Register #(.width(32)) register_5 (.D(rd_data), .en(and_5_out), .clk(clock_1_out), .Q(register_5_q));  // open: clr
  Register #(.width(32)) register_6 (.D(rd_data), .en(and_6_out), .clk(clock_1_out), .Q(register_6_q));  // open: clr
  Register #(.width(32)) register_7 (.D(rd_data), .en(and_7_out), .clk(clock_1_out), .Q(register_7_q));  // open: clr
  Register #(.width(32)) register_8 (.D(rd_data), .en(and_8_out), .clk(clock_1_out), .Q(register_8_q));  // open: clr
  and and_9 (and_9_out, write_e, demultiplexer_1_out2);
  and and_10 (and_10_out, write_e, demultiplexer_1_out6);
  and and_11 (and_11_out, write_e, demultiplexer_1_out10);
  and and_12 (and_12_out, write_e, demultiplexer_1_out14);
  and and_13 (and_13_out, write_e, demultiplexer_1_out18);
  and and_14 (and_14_out, write_e, demultiplexer_1_out22);
  and and_15 (and_15_out, write_e, demultiplexer_1_out26);
  and and_16 (and_16_out, write_e, demultiplexer_1_out30);
  Register #(.width(32)) register_9 (.D(rd_data), .en(and_9_out), .clk(clock_1_out), .Q(register_9_q));  // open: clr
  Register #(.width(32)) register_10 (.D(rd_data), .en(and_10_out), .clk(clock_1_out), .Q(register_10_q));  // open: clr
  Register #(.width(32)) register_11 (.D(rd_data), .en(and_11_out), .clk(clock_1_out), .Q(register_11_q));  // open: clr
  Register #(.width(32)) register_12 (.D(rd_data), .en(and_12_out), .clk(clock_1_out), .Q(register_12_q));  // open: clr
  Register #(.width(32)) register_13 (.D(rd_data), .en(and_13_out), .clk(clock_1_out), .Q(register_13_q));  // open: clr
  Register #(.width(32)) register_14 (.D(rd_data), .en(and_14_out), .clk(clock_1_out), .Q(register_14_q));  // open: clr
  Register #(.width(32)) register_15 (.D(rd_data), .en(and_15_out), .clk(clock_1_out), .Q(register_15_q));  // open: clr
  Register #(.width(32)) register_16 (.D(rd_data), .en(and_16_out), .clk(clock_1_out), .Q(register_16_q));  // open: clr
  and and_17 (and_17_out, write_e, demultiplexer_1_out3);
  and and_18 (and_18_out, write_e, demultiplexer_1_out7);
  and and_19 (and_19_out, write_e, demultiplexer_1_out11);
  and and_20 (and_20_out, write_e, demultiplexer_1_out15);
  and and_21 (and_21_out, write_e, demultiplexer_1_out19);
  and and_22 (and_22_out, write_e, demultiplexer_1_out23);
  and and_23 (and_23_out, write_e, demultiplexer_1_out27);
  and and_24 (and_24_out, write_e, demultiplexer_1_out31);
  Register #(.width(32)) register_17 (.D(rd_data), .en(and_17_out), .clk(clock_1_out), .Q(register_17_q));  // open: clr
  Register #(.width(32)) register_18 (.D(rd_data), .en(and_18_out), .clk(clock_1_out), .Q(register_18_q));  // open: clr
  Register #(.width(32)) register_19 (.D(rd_data), .en(and_19_out), .clk(clock_1_out), .Q(register_19_q));  // open: clr
  Register #(.width(32)) register_20 (.D(rd_data), .en(and_20_out), .clk(clock_1_out), .Q(register_20_q));  // open: clr
  Register #(.width(32)) register_21 (.D(rd_data), .en(and_21_out), .clk(clock_1_out), .Q(register_21_q));  // open: clr
  Register #(.width(32)) register_22 (.D(rd_data), .en(and_22_out), .clk(clock_1_out), .Q(register_22_q));  // open: clr
  Register #(.width(32)) register_23 (.D(rd_data), .en(and_23_out), .clk(clock_1_out), .Q(register_23_q));  // open: clr
  Register #(.width(32)) register_24 (.D(rd_data), .en(and_24_out), .clk(clock_1_out), .Q(register_24_q));  // open: clr
  Register #(.width(32)) register_25 (.D(rd_data), .en(and_25_out), .clk(clock_1_out), .Q(register_25_q));  // open: clr
  and and_25 (and_25_out, write_e, demultiplexer_1_out4);
  Register #(.width(32)) register_26 (.D(rd_data), .en(and_26_out), .clk(clock_1_out), .Q(register_26_q));  // open: clr
  and and_26 (and_26_out, write_e, demultiplexer_1_out8);
  Register #(.width(32)) register_27 (.D(rd_data), .en(and_27_out), .clk(clock_1_out), .Q(register_27_q));  // open: clr
  and and_27 (and_27_out, write_e, demultiplexer_1_out12);
  Register #(.width(32)) register_28 (.D(rd_data), .en(and_28_out), .clk(clock_1_out), .Q(register_28_q));  // open: clr
  and and_28 (and_28_out, write_e, demultiplexer_1_out16);
  Register #(.width(32)) register_29 (.D(rd_data), .en(and_29_out), .clk(clock_1_out), .Q(register_29_q));  // open: clr
  and and_29 (and_29_out, write_e, demultiplexer_1_out20);
  Register #(.width(32)) register_30 (.D(rd_data), .en(and_30_out), .clk(clock_1_out), .Q(register_30_q));  // open: clr
  and and_30 (and_30_out, write_e, demultiplexer_1_out24);
  Register #(.width(32)) register_31 (.D(rd_data), .en(and_31_out), .clk(clock_1_out), .Q(register_31_q));  // open: clr
  and and_31 (and_31_out, write_e, demultiplexer_1_out28);
  Multiplexer #(.select(5), .width(32)) multiplexer_1 (
    .in0({32{1'b0}}), .in1(register_1_q), .in2(register_9_q), .in3(register_17_q), .in4(register_25_q),
    .in5(register_2_q), .in6(register_10_q), .in7(register_18_q), .in8(register_26_q), .in9(register_3_q),
    .in10(register_11_q), .in11(register_19_q), .in12(register_27_q), .in13(register_4_q),
    .in14(register_12_q), .in15(register_20_q), .in16(register_28_q), .in17(register_5_q),
    .in18(register_13_q), .in19(register_21_q), .in20(register_29_q), .in21(register_6_q),
    .in22(register_14_q), .in23(register_22_q), .in24(register_30_q), .in25(register_7_q),
    .in26(register_15_q), .in27(register_23_q), .in28(register_31_q), .in29(register_8_q),
    .in30(register_16_q), .in31(register_24_q), .out(rs_data), .sel(rs));
  Multiplexer #(.select(5), .width(32)) multiplexer_2 (
    .in1(register_1_q), .in2(register_9_q), .in3(register_17_q), .in4(register_25_q), .in5(register_2_q),
    .in6(register_10_q), .in7(register_18_q), .in8(register_26_q), .in9(register_3_q), .in10(register_11_q),
    .in11(register_19_q), .in12(register_27_q), .in13(register_4_q), .in14(register_12_q),
    .in15(register_20_q), .in16(register_28_q), .in17(register_5_q), .in18(register_13_q),
    .in19(register_21_q), .in20(register_29_q), .in21(register_6_q), .in22(register_14_q),
    .in23(register_22_q), .in24(register_30_q), .in25(register_7_q), .in26(register_15_q),
    .in27(register_23_q), .in28(register_31_q), .in29(register_8_q), .in30(register_16_q),
    .in31(register_24_q), .out(rt_data), .sel(rt));  // open: in0

  // Notes on the sheet:
  //   Tyeon Ford and Andy Quach
endmodule

module ALU (
  input  [3:0] ALU_CODE,
  input  [31:0] OP1,
  input  [31:0] OP2,
  output [31:0] Res
);

  wire clock_1_out, comparator_1_lt, comparator_2_eq, comparator_3_eq, or_2_out;
  wire [4:0] bit_extender_1_out, bit_extender_2_out;
  wire [31:0] adder_1_out, and_1_out, bit_extender_3_out, divider_1_out, divider_1_rem, HI_q, LO_q,
       multiplexer_1_out, multiplexer_2_out, multiplier_1_cout, multiplier_1_out, nor_1_out, or_1_out,
       shifter_1_out, shifter_2_out, subtractor_1_out, xor_1_out;

  Clock clock_1 (.out(clock_1_out));
  Bit_Extender #(.in_width(32), .out_width(5), .\type ("zero")) bit_extender_1 (.in(OP2), .out(bit_extender_1_out));
  Bit_Extender #(.in_width(32), .out_width(5), .\type ("zero")) bit_extender_2 (.in(OP2), .out(bit_extender_2_out));
  Adder #(.width(32)) adder_1 (.a(OP1), .b(OP2), .out(adder_1_out));  // open: cin, cout
  Subtractor #(.width(32)) subtractor_1 (.a(OP1), .b(OP2), .out(subtractor_1_out));  // open: bin, bout
  Shifter #(.width(32)) shifter_1 (.in(OP1), .\dist (bit_extender_1_out), .out(shifter_1_out));
  Shifter #(.shift("lr"), .width(32)) shifter_2 (.in(OP1), .\dist (bit_extender_2_out), .out(shifter_2_out));
  Comparator #(.width(32)) comparator_1 (.a(OP1), .b(OP2), .lt(comparator_1_lt));  // open: gt, eq
  assign and_1_out = OP1 & OP2;  // AND_Gate and_1, 32 bits wide
  assign or_1_out = OP1 | OP2;  // OR_Gate or_1, 32 bits wide
  assign nor_1_out = ~(OP1 | OP2);  // NOR_Gate nor_1, 32 bits wide
  assign xor_1_out = OP1 ^ OP2;  // XOR_Gate xor_1, 32 bits wide
  Multiplier #(.width(32)) multiplier_1 (
    .a(OP1), .b(OP2), .out(multiplier_1_out), .cout(multiplier_1_cout));  // open: cin
  Divider #(.width(32)) divider_1 (.a(OP1), .b(OP2), .out(divider_1_out), .rem(divider_1_rem));  // open: upper
  assign bit_extender_3_out = {{31{1'b0}}, comparator_1_lt};  // Bit_Extender bit_extender_3
  Multiplexer #(.width(32)) multiplexer_1 (
    .in0(multiplier_1_out), .in1(divider_1_out), .out(multiplexer_1_out), .sel(comparator_3_eq));
  Multiplexer #(.width(32)) multiplexer_2 (
    .in0(multiplier_1_cout), .in1(divider_1_rem), .out(multiplexer_2_out), .sel(comparator_3_eq));
  Comparator #(.width(4)) comparator_2 (.a(ALU_CODE), .b(4'b0010), .eq(comparator_2_eq));  // open: gt, lt
  Comparator #(.width(4)) comparator_3 (.a(ALU_CODE), .b(4'b0011), .eq(comparator_3_eq));  // open: gt, lt
  or or_2 (or_2_out, comparator_2_eq, comparator_3_eq);
  Register #(.width(32)) LO (.D(multiplexer_1_out), .en(or_2_out), .clk(clock_1_out), .Q(LO_q));  // open: clr
  Register #(.width(32)) HI (.D(multiplexer_2_out), .en(or_2_out), .clk(clock_1_out), .Q(HI_q));  // open: clr
  Multiplexer #(.select(4), .width(32)) multiplexer_3 (
    .in0(adder_1_out), .in1(subtractor_1_out), .in4(LO_q), .in5(HI_q), .in6(shifter_1_out),
    .in7(shifter_2_out), .in8(bit_extender_3_out), .in9(and_1_out), .in10(or_1_out), .in11(nor_1_out),
    .in12(xor_1_out), .out(Res), .sel(ALU_CODE));  // open: in2, in3, in13, in14, in15

  // Notes on the sheet:
  //   Andy Quach and Tyeon Ford
  //   add
  //   subtract
  //   sll
  //   srl
  //   AND (2)
  //   OR (2)
  //   slt
  //   NOR (2)
  //   XOR (2)
  //   Product
  //   Overflow
  //   Quotient
  //   Remainder
endmodule

module Control (
  input  [31:0] Inst,
  output [4:0] rs,
  output [4:0] rt,
  output [4:0] rd,
  output [31:0] imm,
  output reg_write_e,
  output imm_sel,
  output [3:0] ALU_code
);
endmodule
